// Logisim project Circuit.circ as structural Verilog: 1 circuit, main circuit main
module main (
  input  X0,
  input  X1,
  input  X2,
  output out_4
);

  wire and_1_out, and_2_out, not_1_out, not_2_out, or_1_out;

  not not_1 (not_1_out, X1);
  not not_2 (not_2_out, or_1_out);
  or or_1 (or_1_out, X0, X2);
  and and_1 (and_1_out, not_1_out, X2);
  and and_2 (and_2_out, not_2_out, X1);
  or or_2 (out_4, and_2_out, and_1_out);
endmodule
