// Logisim project mycircuit.circ as structural Verilog: 1 circuit, main circuit main
module main (
  input  X0,
  input  X1,
  input  X3,
  input  X2,
  output out_5
);

  wire and_1_out, xor_1_out;

  and and_1 (and_1_out, X0, X0, X1);
  xor xor_1 (xor_1_out, X1, X0);
  Multiplexer #(.select(2)) multiplexer_1 (
    .in0(and_1_out), .in1(X0), .in2(X1), .in3(xor_1_out), .out(out_5), .sel({X3, X2}));  // open: en
endmodule
