// Logisim project my_fsm.circ as structural Verilog: 1 circuit, main circuit main
module main (
  input  \input ,
  input  Clock,
  output out0,
  output out1
);

  wire and_1_out, and_2_out, and_3_out, and_4_out, and_5_out, and_6_out, and_7_out, and_8_out, and_9_out,
       and_10_out, and_11_out, and_12_out, and_13_out, and_14_out, decoder_1_out0, decoder_1_out1,
       decoder_1_out2, decoder_1_out3, decoder_1_out4, decoder_1_out5, decoder_1_out6, decoder_1_out7,
       not_1_out, or_3_out, or_4_out, or_5_out, or_6_out;
  wire [2:0] d_ff_3_q;

  Decoder #(.select(3)) decoder_1 (
    .out0(decoder_1_out0), .out1(decoder_1_out1), .out2(decoder_1_out2), .out3(decoder_1_out3),
    .out4(decoder_1_out4), .out5(decoder_1_out5), .out6(decoder_1_out6), .out7(decoder_1_out7), .sel(d_ff_3_q));  // open: en
  not not_1 (not_1_out, \input );
  and and_1 (and_1_out, decoder_1_out1, \input );
  and and_2 (and_2_out, decoder_1_out3, \input , \input );
  and and_3 (and_3_out, decoder_1_out4, \input );
  and and_4 (and_4_out, decoder_1_out7, \input );
  and and_5 (and_5_out, decoder_1_out7, \input );
  and and_6 (and_6_out, decoder_1_out6, not_1_out);
  or or_1 (out0, decoder_1_out4, decoder_1_out7);
  or or_2 (out1, decoder_1_out4, decoder_1_out3);
  and and_7 (and_7_out, decoder_1_out2, \input );
  or or_3 (or_3_out, and_5_out, and_6_out);
  or or_4 (or_4_out, decoder_1_out5, decoder_1_out6, and_7_out);
  or or_5 (or_5_out, decoder_1_out2, or_3_out, and_1_out, and_3_out, and_2_out, and_4_out, and_4_out);
  D_Flip_Flop d_ff_1 (.clk(Clock), .D(or_4_out), .Q(d_ff_3_q[2]));  // open: Qn, preset, en, reset
  D_Flip_Flop d_ff_2 (.clk(Clock), .D(or_5_out), .Q(d_ff_3_q[1]));  // open: Qn, preset, en, reset
  and and_8 (and_8_out, decoder_1_out1, not_1_out);
  and and_9 (and_9_out, decoder_1_out2, not_1_out);
  and and_10 (and_10_out, decoder_1_out3, not_1_out);
  and and_11 (and_11_out, decoder_1_out4, not_1_out);
  and and_12 (and_12_out, decoder_1_out5, decoder_1_out5, \input );
  and and_13 (and_13_out, decoder_1_out0, not_1_out);
  and and_14 (and_14_out, decoder_1_out7, not_1_out);
  or or_6 (or_6_out, and_13_out, and_8_out, and_9_out, and_10_out, decoder_1_out6, and_14_out, and_11_out, and_12_out);
  D_Flip_Flop d_ff_3 (.clk(Clock), .D(or_6_out), .Q(d_ff_3_q[0]));  // open: Qn, preset, en, reset
endmodule
